# Fritzing sketch wifi homekit persiana (saved by Fritzing 0.9.3b)

parts:
  U1 = ESP8266 WiFi Module [part_number=ESP8266]
  LM1117_3_3v2 = Voltage Regulator - 5V [package="DPak [SMD]"]
  2K2 = Resistor [tolerance=±5% resistance=2.2k package=THT]
  KY-3 = Keyes Relay [package=THT]
  KY-4 = Keyes Relay [package=THT]
  Power_plug1 = Power plug
  S1 = Square Pushbutton
  S2 = Square Pushbutton
  R1 = Resistor [tolerance=±5% resistance=10k package=THT]
  R2 = Resistor [tolerance=±5% resistance=10k package=THT]
  U2 = mystery part, 3 pins [chip_label=?]
  D1 = Rectifier Diode [part_number=1N4001 package="300 mil [THT]"]
  S3 = Pushbutton [package="[THT]"]
  R3 = Resistor [tolerance=±5% resistance=10k package=THT]

nets:
  N1: U1.VCC, 2K2.Pin_0
  N2: U1.GPIO_0, S1.leg0, R1.Pin_1
  N3: U1.GPIO_16, KY-3.signal
  N4: U1.GPIO_2, D1.cathode
  N5: U1.CH_PD, 2K2.Pin_1
  GND: U1.GND, U1.GPIO_15, LM1117_3_3v2.input_voltage, KY-3.ground, KY-4.ground, Power_plug1.GND, S1.leg1, S2.leg1, U2.pin3, S3.Pin_1, S3.Pin_2
  N6: U1.GPIO_12, KY-4.signal
  N7: U1.GPIO_13, S3.Pin_3, S3.Pin_4, R3.Pin_0
  N8: U1.GPIO_14, S2.leg0, R2.Pin_1
  N9: LM1117_3_3v2.GND, KY-3.power, KY-4.power, R1.Pin_0, R2.Pin_0, R3.Pin_1
  N10: LM1117_3_3v2.output_voltage, Power_plug1.VCC, U2.pin2
  N11: U2.pin1, D1.anode

notes:
  LM1117 3,3v
  ESP8266 03
  2k2
  Sensor Hall
  1N4007
  10K
  Rele Subir
  Rele Bajar
  Pulsador Subir
  Pulsador Bajar
  Modulos Rele 3,3V
  Pulsador Reset
  5 V

custom parts:
  ESP8266 WiFi Module: Generic WiFi Module based on the ESP8266 with onboard PCB antenna and UART communications
  Keyes Relay: The Keyes 5V relay module is suitable for SCM development, home appliance control. It uses a 5V~12V TIL control signal which can control DC / AC signal.
